# Fritzing sketch PiGpioOccupation (saved by Fritzing 0.9.3b)

parts:
  Raspberry_Pi_1 = Raspberry Pi 3 [part_number=RPI-3-V1.2]
  J1 = Basic Servo  # not connected
  M1 = DC Motor

nets:
  N1: Raspberry_Pi_1.GPIO4, M1.pin_2
  N2: Raspberry_Pi_1.GND, M1.pin_1
