# Fritzing sketch PiGpioOccupationCurrent (saved by Fritzing 0.9.3b)

parts:
  J1 = Basic Servo  # not connected
  M1 = DC Motor
  Raspberry_Pi_1 = Raspberry Pi 3 [part_number=RPI-3-V1.2]

nets:
  N1: M1.pin_1, Raspberry_Pi_1.GND
  N2: M1.pin_2, Raspberry_Pi_1.GPIO4
